# Fritzing sketch BatteryHarness (saved by Fritzing 0.8.0b)
stripboards: 5

parts:
  U1 = Voltage Regulator - 5V [package="TO220 [THT]"]  # not connected
  U2 = Voltage Regulator - 5V [package="DPak [SMD]"]  # not connected
  J1 = female pin header, 3 pins [form="♀ (female)"]
  J2 = female pin header, 3 pins [form="♀ (female)"]
  J3 = female pin header, 3 pins [form="♀ (female)"]
  U3 = Voltage Regulator - 5V [package="DPak [SMD]"]  # not connected
  C2 = Ceramic Capacitor [capacitance=100nF package="100 mil [THT, multilayer]"]
  J5 = female pin header, 7 pins [form="♀ (female)"]
  J4 = female pin header, 7 pins [form="♀ (female)"]
  J6 = female pin header, 3 pins [form="♀ (female)"]
  J9 = female pin header, 3 pins [form="♀ (female)"]
  J17 = male pin header, 2 pins [form="♂ (male)"]  # not connected
  J18 = male pin header, 2 pins [form="♂ (male)"]  # not connected
  C3 = Ceramic Capacitor [capacitance=330nF package="100 mil [THT, multilayer]"]
  J19 = male pin header, 4 pins [form="♂ (male)"]
  J20 = male pin header, 4 pins [form="♂ (male)"]
  J13 = male pin header, 5 pins [form="♂ (male)"]
  J12 = male pin header, 5 pins [form="♂ (male)"]
  J15 = male pin header, 2 pins [form="♂ (male)"]
  J16 = female pin header, 4 pins [form="♀ (female)"]
  J21 = female pin header, 4 pins [form="♀ (female)"]
  J22 = male pin header, 2 pins [form="♂ (male)"]
  J8 = male pin header, 3 pins [form="♂ (male)"]
  J7 = male pin header, 3 pins [form="♂ (male)"]
  J23 = male pin header, 3 pins [form="♂ (male)"]
  J24 = female pin header, 3 pins [form="♀ (female)"]
  J25 = female pin header, 4 pins [form="♀ (female)"]
  J26 = female pin header, 4 pins [form="♀ (female)"]
  J27 = female pin header, 4 pins [form="♀ (female)"]

nets:
  N1: J1.pin1, J19.pin1, J20.pin1, J16.pin4, J21.pin4
  N2: J1.pin2, J2.pin2, J3.pin1, C2.0, J6.pin1, J9.pin1, C3.0, J19.pin2, J20.pin2, J12.pin5, J8.pin1, J7.pin1, J23.pin1, J24.pin1, J25.pin2, J26.pin2, J27.pin2
  N3: J1.pin3, J6.pin3, J9.pin3, J8.pin3, J7.pin3, J23.pin3, J24.pin3, J25.pin1, J26.pin1, J27.pin1
  N4: J2.pin3, J13.pin5
  N5: J3.pin2, C3.1
  N6: J3.pin3, C2.1, J19.pin3, J20.pin3
  N7: J5.pin1, J5.pin2, J5.pin3
  N8: J4.pin1, J4.pin2, J4.pin3
  N9: J6.pin2, J7.pin2
  N10: J9.pin2, J8.pin2
  N11: J15.pin1, J21.pin1
  N12: J15.pin2, J21.pin2, J21.pin3
  N13: J16.pin1, J22.pin1
  N14: J16.pin2, J16.pin3, J22.pin2
  N15: J23.pin2, J24.pin2

notes:
  ribbon
  I-bridges
  8V cells
  IR
  Loading servo
  H-bridges/servos
  Lasers
  QRD
  Power
