# Fritzing sketch BatteryHarness2 (saved by Fritzing 0.8.0b)
stripboards: 10

parts:
  U1 = Voltage Regulator - 5V [package="TO220 [THT]"]  # not connected
  U2 = Voltage Regulator - 5V [package="DPak [SMD]"]  # not connected
  J1 = female pin header, 3 pins [form="♀ (female)"]
  J2 = female pin header, 3 pins [form="♀ (female)"]
  J3 = female pin header, 3 pins [form="♀ (female)"]
  U3 = Voltage Regulator - 5V [package="DPak [SMD]"]  # not connected
  C2 = Ceramic Capacitor [capacitance=100nF package="100 mil [THT, multilayer]"]
  J5 = female pin header, 7 pins [form="♀ (female)"]
  J4 = female pin header, 7 pins [form="♀ (female)"]
  J6 = female pin header, 3 pins [form="♀ (female)"]
  J9 = female pin header, 3 pins [form="♀ (female)"]
  J17 = male pin header, 2 pins [form="♂ (male)"]  # not connected
  J18 = male pin header, 2 pins [form="♂ (male)"]  # not connected
  C3 = Ceramic Capacitor [capacitance=330nF package="100 mil [THT, multilayer]"]
  J19 = male pin header, 4 pins [form="♂ (male)"]
  J20 = male pin header, 4 pins [form="♂ (male)"]
  J13 = male pin header, 5 pins [form="♂ (male)"]
  J12 = male pin header, 5 pins [form="♂ (male)"]
  J15 = male pin header, 2 pins [form="♂ (male)"]
  J16 = female pin header, 4 pins [form="♀ (female)"]
  J21 = female pin header, 4 pins [form="♀ (female)"]
  J22 = male pin header, 2 pins [form="♂ (male)"]
  J8 = male pin header, 3 pins [form="♂ (male)"]
  J7 = male pin header, 3 pins [form="♂ (male)"]
  J23 = male pin header, 3 pins [form="♂ (male)"]
  J24 = female pin header, 3 pins [form="♀ (female)"]
  J25 = female pin header, 4 pins [form="♀ (female)"]  # not connected
  J26 = female pin header, 4 pins [form="♀ (female)"]  # not connected
  J27 = female pin header, 4 pins [form="♀ (female)"]  # not connected
  J28 = female pin header, 3 pins [form="♀ (female)"]
  J29 = female pin header, 3 pins [form="♀ (female)"]
  J30 = female pin header, 3 pins [form="♀ (female)"]
  J31 = female pin header, 3 pins [form="♀ (female)"]
  J32 = male pin header, 2 pins [form="♂ (male)"]
  C4 = Ceramic Capacitor [capacitance=100nF package="100 mil [THT, multilayer]"]
  J33 = male pin header, 2 pins [form="♂ (male)"]
  J34 = female pin header, 7 pins [form="♀ (female)"]
  J35 = female pin header, 7 pins [form="♀ (female)"]
  J37 = male pin header, 3 pins [form="♂ (male)"]
  J38 = male pin header, 3 pins [form="♂ (male)"]
  J36 = male pin header, 3 pins [form="♂ (male)"]
  J39 = male pin header, 3 pins [form="♂ (male)"]
  J40 = male pin header, 3 pins [form="♂ (male)"]
  J41 = male pin header, 3 pins [form="♂ (male)"]
  J42 = male pin header, 3 pins [form="♂ (male)"]
  S1 = Toggle Switch [package=THT]
  S2 = Toggle Switch [package=THT]
  J43 = male pin header, 5 pins [form="♂ (male)"]
  J44 = male pin header, 5 pins [form="♂ (male)"]
  J45 = female pin header, 4 pins [form="♀ (female)"]
  J46 = female pin header, 4 pins [form="♀ (female)"]
  J47 = male pin header, 2 pins [form="♂ (male)"]
  J48 = male pin header, 2 pins [form="♂ (male)"]
  J49 = male pin header, 5 pins [form="♂ (male)"]
  J50 = male pin header, 4 pins [form="♂ (male)"]
  J51 = female pin header, 4 pins [form="♀ (female)"]

nets:
  N1: J1.pin1, J19.pin1, J20.pin1, J16.pin4, J21.pin4
  N2: J1.pin2, J2.pin2, J3.pin1, C2.0, J6.pin1, J9.pin1, C3.0, J19.pin2, J20.pin2, J12.pin5, J8.pin1, J7.pin1, J23.pin1, J24.pin1
  N3: J1.pin3, J6.pin3, J9.pin3, J8.pin3, J7.pin3, J23.pin3, J24.pin3
  N4: J2.pin3, J13.pin5
  N5: J3.pin2, C3.1
  N6: J3.pin3, C2.1, J19.pin3, J20.pin3
  N7: J5.pin1, J5.pin2, J5.pin3
  N8: J4.pin1, J4.pin2, J4.pin3
  N9: J6.pin2, J7.pin2
  N10: J9.pin2, J8.pin2
  N11: J15.pin1, J16.pin1
  N12: J15.pin2, J16.pin2, J16.pin3
  N13: J21.pin1, J22.pin1
  N14: J21.pin2, J21.pin3, J22.pin2
  N15: J23.pin2, J24.pin2
  N16: J28.pin1, J31.pin1, J34.pin7, J35.pin7, J45.pin4, J46.pin4
  N17: J28.pin2, J29.pin2, J30.pin1, J31.pin2, J32.pin2, C4.0, J33.pin1, J34.pin5, J35.pin5, J37.pin1, J38.pin1, J36.pin1, J39.pin1, J40.pin1, J41.pin1, J42.pin1, J44.pin5, J49.pin4, J50.pin3, J51.pin2
  N18: J28.pin3, J31.pin3, J34.pin6, J35.pin6, J37.pin2, J38.pin2, J36.pin2, J39.pin2, J40.pin2, J41.pin2, J42.pin2, J51.pin1
  N19: J29.pin1, S2.COM
  N20: J29.pin3, J43.pin5, J49.pin5, J50.pin4
  N21: J30.pin2, S1.COM
  N22: J30.pin3, C4.1, J49.pin3, J50.pin2
  N23: J32.pin1, S2.L1
  N24: J33.pin2, S1.L1
  N25: J34.pin1, J34.pin2, J34.pin3
  N26: J35.pin1, J35.pin2, J35.pin3
  N27: J37.pin3, J36.pin3
  N28: J38.pin3, J39.pin3
  N29: J40.pin3, J41.pin3, J42.pin3
  N30: J45.pin1, J47.pin1
  N31: J45.pin2, J45.pin3, J47.pin2
  N32: J46.pin1, J48.pin1
  N33: J46.pin2, J46.pin3, J48.pin2
  N34: J49.pin2, J50.pin1

notes:
  ribbon
  I-bridges
  8V cells
  IR
  Loading servo
  H-bridges/servos
  lasers
  QRD
  Power
