# Fritzing sketch H-bridge-real (saved by Fritzing 0.8.0b)
stripboards: 4

parts:
  IC1 = DIP - 8 pins [chip_label=LM311 package="DIP (Dual Inline) [THT]"]
  IC2 = DIP - 8 pins [chip_label=LM311 package="DIP (Dual Inline) [THT]"]
  Q1 = Basic FET P-Channel [package="TO220 [THT]"]
  Q2 = Basic FET P-Channel [package="TO220 [THT]"]
  Q4 = Basic FET N-Channel [package="TO220 [THT]"]
  Q3 = Basic FET N-Channel [package="TO220 [THT]"]
  Q5 = NPN-Transistor [package="TO92 [THT]"]
  Q6 = NPN-Transistor [package="TO92 [THT]"]
  Q7 = PNP-Transistor [package="TO92 [THT]"]
  Q8 = PNP-Transistor [package="TO92 [THT]"]
  R1 = Resistor [tolerance=±5% resistance=100 package=THT]
  R2 = Resistor [tolerance=±5% resistance=100 package=THT]
  R3 = Resistor [tolerance=±5% resistance=100 package=THT]
  R4 = Resistor [tolerance=±5% resistance=100 package=THT]
  R5 = Resistor [tolerance=±5% resistance=10k package=THT]
  R6 = Resistor [tolerance=±5% resistance=10k package=THT]
  R7 = Resistor [tolerance=±5% resistance=10k package=THT]
  R8 = Resistor [tolerance=±5% resistance=10k package=THT]
  R9 = Resistor [tolerance=±5% resistance=33k package=THT]
  R10 = Resistor [tolerance=±5% resistance=33k package=THT]
  R11 = Resistor [tolerance=±5% resistance=33k package=THT]
  R12 = Resistor [tolerance=±5% resistance=33k package=THT]

nets:
  GND: IC1.GND, IC1.VEE, IC2.GND, IC2.VEE, Q4.source, Q3.source, Q5.E, Q6.E, R5.Pin_1, R6.Pin_1
  5V: IC1.IN-, IC1.VCC, IC2.IN-, IC2.VCC, R10.Pin_1, R11.Pin_1
  N1: IC1.OUT, Q5.B, R11.Pin_0
  N2: IC2.OUT, Q6.B, R10.Pin_0
  N3: Q1.gate, R2.Pin_1, R7.Pin_1, R12.Pin_1
  N4: Q1.drain, Q3.drain
  12V: Q1.source, Q2.source, Q7.E, Q8.E, R7.Pin_0, R8.Pin_0
  N5: Q2.gate, R1.Pin_1, R8.Pin_1, R9.Pin_1
  N6: Q2.drain, Q4.drain
  N7: Q4.gate, R4.Pin_1, R5.Pin_0
  N8: Q3.gate, R3.Pin_1, R6.Pin_0
  N9: Q5.C, R2.Pin_0
  N10: Q6.C, R1.Pin_0
  N11: Q7.B, R9.Pin_0
  N12: Q7.C, R3.Pin_0
  N13: Q8.B, R12.Pin_0
  N14: Q8.C, R4.Pin_0

custom parts:
  DIP - 8 pins: A DIP stand-in part for whatever IC you want. With 8 pins on a 300mil dual inline package (DIP) footprint.
