# Fritzing sketch H-bridge (saved by Fritzing 0.8.0b)
stripboards: 4

parts:
  IC1 = DIP - 8 pins [chip_label=LM311 package="DIP (Dual Inline) [THT]"]
  IC2 = DIP - 8 pins [chip_label=LM311 package="DIP (Dual Inline) [THT]"]
  R1 = Resistor [tolerance=±5% resistance=33k package=THT]
  R2 = Resistor [tolerance=±5% resistance=33k package=THT]
  Q1 = Basic FET P-Channel [package="TO220 [THT]"]  # not connected
  Q2 = Basic FET N-Channel [package="TO220 [THT]"]  # not connected
  R3 = Resistor [tolerance=±5% resistance=10k package=THT]
  Q3 = PNP-Transistor [package="TO92 [THT]"]
  R4 = Resistor [tolerance=±5% resistance=100 package=THT]
  Q4 = NPN-Transistor [package="TO92 [THT]"]
  R5 = Resistor [tolerance=±5% resistance=100 package=THT]
  R8 = Resistor [tolerance=±5% resistance=10k package=THT]
  R9 = Resistor [tolerance=±5% resistance=10k package=THT]
  Q5 = PNP-Transistor [package="TO92 [THT]"]
  R10 = Resistor [tolerance=±5% resistance=100 package=THT]
  Q6 = NPN-Transistor [package="TO92 [THT]"]
  R11 = Resistor [tolerance=±5% resistance=100 package=THT]
  R12 = Resistor [tolerance=±5% resistance=10k package=THT]
  Q7 = Basic FET N-Channel [package="TO220 [THT]"]  # not connected
  Q8 = Basic FET P-Channel [package="TO220 [THT]"]  # not connected
  R13 = Resistor [tolerance=±5% resistance=33k package=THT]
  R14 = Resistor [tolerance=±5% resistance=33k package=THT]

nets:
  GND: IC1.GND, IC1.VEE, IC2.GND, IC2.VEE, R3.Pin_1, Q4.E, R8.Pin_0, R9.Pin_1, Q6.E, R12.Pin_0
  VCC: IC1.IN-, IC1.VCC, IC2.IN-, IC2.VCC, R1.Pin_0, R2.Pin_0
  N1: IC1.OUT, R2.Pin_1, Q4.B
  N2: IC2.OUT, R1.Pin_1, Q6.B
  N3: R3.Pin_0, R4.Pin_0
  N4: Q3.E, Q5.E
  N5: Q3.B, R13.Pin_0
  N6: Q3.C, R4.Pin_1
  N7: Q4.C, R5.Pin_1
  N8: R5.Pin_0, R8.Pin_1, R14.Pin_0
  N9: R9.Pin_0, R10.Pin_0
  N10: Q5.B, R14.Pin_1
  N11: Q5.C, R10.Pin_1
  N12: Q6.C, R11.Pin_1
  N13: R11.Pin_0, R12.Pin_1, R13.Pin_1

custom parts:
  DIP - 8 pins: A DIP stand-in part for whatever IC you want. With 8 pins on a 300mil dual inline package (DIP) footprint.
