# Fritzing sketch IR detection circuit (saved by Fritzing 0.8.0b)
stripboards: 3

parts:
  Q1 = NPN-Transistor [package="TO92 [THT]"]
  C1 = Ceramic Capacitor [capacitance=470pF package="200 mil [THT, multilayer]"]
  IC4 = DIP - 8 pins [chip_label=TL082 package="DIP (Dual Inline) [THT]"]
  R3 = Resistor [tolerance=±5% resistance=10k package=THT]
  R5 = Resistor [tolerance=±5% resistance=1.6M package=THT]
  C2 = Ceramic Capacitor [capacitance=0.1nF package="100 mil [THT, multilayer]"]
  R6 = Resistor [tolerance=±5% resistance=1.6M package=THT]
  C3 = Ceramic Capacitor [capacitance=0.1nF package="100 mil [THT, multilayer]"]
  R7 = Resistor [tolerance=±5% resistance=1.6M package=THT]
  IC6 = DIP - 8 pins [chip_label=TL082 package="DIP (Dual Inline) [THT]"]
  D1 = Zener Diode [part_number=1N4732A breakdown_voltage=3.6V package="300 mil [THT]"]
  D2 = Zener Diode [part_number=1N4732A breakdown_voltage=3.6V package="300 mil [THT]"]
  R2 = Resistor [tolerance=±5% resistance=47k package=THT]
  R1 = Resistor [tolerance=±5% resistance=500 package=THT]
  R10 = Rotary Potentiometer (Small)
  C4 = Ceramic Capacitor [capacitance=0.1nF package="100 mil [THT, multilayer]"]
  C6 = Ceramic Capacitor [capacitance=22nF package="100 mil [THT, multilayer]"]
  R11 = Resistor [tolerance=±5% resistance=30k package=THT]
  IC3 = DIP - 8 pins [chip_label=TL082 package="DIP (Dual Inline) [THT]"]
  IC7 = DIP - 8 pins [chip_label=TL082 package="DIP (Dual Inline) [THT]"]
  C7 = Ceramic Capacitor [capacitance=0.1nF package="100 mil [THT, multilayer]"]
  R14 = Resistor [tolerance=±5% resistance=1.6M package=THT]

nets (from the schematic view):
  N1: Q1.E, R1.Pin_0, IC3.1IN+
  9V: Q1.C, IC4.VCC+, IC6.VCC+, IC3.VCC+, IC7.VCC+
  N2: C1.0, R2.Pin_0, IC3.2IN+
  N3: C1.1, IC3.1OUT, IC3.1IN-
  N4: IC4.1OUT, IC4.2IN+, R10.wiper
  N5: IC4.1IN-, R3.Pin_1, R10.leg1
  GND: IC4.1IN+, IC4.VCC-, IC6.VCC-, D2.anode, R2.Pin_1, R1.Pin_1, C6.0, R11.Pin_0, IC3.VCC-, IC7.1IN+, IC7.VCC-, IC7.2IN+
  N6: IC4.2IN-, IC4.2OUT, R5.Pin_0
  N7: R3.Pin_0, IC3.2IN-, IC3.2OUT
  N8: R5.Pin_1, C2.1
  N9: C2.0, R6.Pin_1, C3.1, IC7.1IN-
  N10: R6.Pin_0, C3.0, R7.Pin_1, IC7.1OUT
  N11: R7.Pin_0, C4.1
  N12: IC6.1OUT, D1.anode
  N13: IC6.1IN-, IC6.2IN+, D1.cathode, C6.1, R11.Pin_1
  N14: IC6.1IN+, R14.Pin_1
  N15: IC6.2IN-, IC6.2OUT, D2.cathode
  N16: C4.0, IC7.2OUT, C7.1, R14.Pin_0

notes:
  Output
  Input

custom parts:
  DIP - 8 pins: A DIP stand-in part for whatever IC you want. With 8 pins on a 300mil dual inline package (DIP) footprint.
