# Fritzing sketch IR sensor (saved by Fritzing 0.8.0b)
stripboards: 6

parts:
  Q1 = NPN-Transistor [package="TO92 [THT]"]
  R1 = Resistor [tolerance=±5% resistance=1k package=THT]
  R2 = Resistor [tolerance=±5% resistance=47k package=THT]
  C3 = Ceramic Capacitor [capacitance=0.47nF package="100 mil [THT, multilayer]"]
  R3 = Resistor [tolerance=±5% resistance=1k package=THT]
  R4 = Resistor [tolerance=±5% resistance=100k package=THT]
  R5 = Resistor [tolerance=±5% resistance=3.3k package=THT]
  C4 = Ceramic Capacitor [capacitance=47nF package="100 mil [THT, multilayer]"]
  C5 = Ceramic Capacitor [capacitance=47nF package="100 mil [THT, multilayer]"]
  R6 = Resistor [tolerance=±5% resistance=3.3k package=THT]
  C6 = Ceramic Capacitor [capacitance=4.7nF package="100 mil [THT, multilayer]"]
  R7 = Resistor [tolerance=±5% resistance=33k package=THT]
  R8 = Resistor [tolerance=±5% resistance=3.3k package=THT]
  C7 = Ceramic Capacitor [capacitance=47nF package="100 mil [THT, multilayer]"]
  D1 = Zener Diode [part_number=1N4732A breakdown_voltage=3.6V package="300 mil [THT]"]
  R9 = Resistor [tolerance=±5% resistance=33k package=THT]
  R10 = Resistor [tolerance=±5% resistance=1k package=THT]
  IC4 = DIP - 8 pins [chip_label=TL082 package="DIP (Dual Inline) [THT]"]
  IC1 = DIP - 8 pins [chip_label=TL082 package="DIP (Dual Inline) [THT]"]
  IC5 = DIP - 8 pins [chip_label=TL082 package="DIP (Dual Inline) [THT]"]
  IC3 = DIP - 8 pins [chip_label=TL082 package="DIP (Dual Inline) [THT]"]
  D2 = Rectifier Diode [part_number=1N4001 package="300 mil [THT]"]
  C9 = Electrolytic Capacitor [capacitance=470nF package="100 mil [THT, electrolytic]"]

nets (from the schematic view):
  N1: Q1.E, R1.Pin_1, IC1.2IN+
  9V: Q1.C, IC4.VCC+, IC1.VCC+, IC5.VCC+, IC3.VCC+
  GND: R1.Pin_0, R2.Pin_0, D1.anode, R9.Pin_1, IC5.1IN+, IC3.1IN+, IC3.2IN+, C9.-
  N2: R2.Pin_1, C3.0, IC1.1IN+
  N3: C3.1, IC1.2IN-, IC1.2OUT
  N4: R3.Pin_0, R4.Pin_1, IC5.1OUT, IC5.2IN+
  N5: R3.Pin_1, IC1.1OUT, IC1.1IN-
  N6: R4.Pin_0, IC5.1IN-
  N7: R5.Pin_0, C4.1
  N8: R5.Pin_1, IC5.2IN-, IC5.2OUT
  N9: C4.0, C5.1, R6.Pin_1, IC3.2IN-
  N10: C5.0, R6.Pin_0, R8.Pin_1, IC3.2OUT
  N11: C6.0, R7.Pin_1, C7.1, IC3.1IN-
  N12: C6.1, R7.Pin_0, IC4.1IN+, IC3.1OUT
  N13: R8.Pin_0, C7.0
  N14: D1.cathode, R10.Pin_0
  N15: R9.Pin_0, IC4.1IN-, IC4.2IN+, D2.cathode, C9.+
  N16: R10.Pin_1, IC4.2IN-, IC4.2OUT
  N17: IC4.1OUT, D2.anode
  -9V: IC4.VCC-, IC1.VCC-, IC5.VCC-, IC3.VCC-

notes:
  output

custom parts:
  DIP - 8 pins: A DIP stand-in part for whatever IC you want. With 8 pins on a 300mil dual inline package (DIP) footprint.
