# Fritzing sketch LM311 Comparator Circuit (saved by Fritzing 0.8.0b)
breadboards: 1

parts:
  IC1 = IC, DIP package, 4 pins [chip_label=QRD]
  R1 = Resistor [tolerance=±5% resistance=10k package=THT]
  R2 = Resistor [tolerance=±5% resistance=220 package=THT]
  R3 = Trimmer Potentiometer [maximum_resistance=100kΩ package=THT]
  U1 = LM 358 Dual Op-Amp [package="DIP8 [THT]"]

nets:
  5V: IC1.pin1, IC1.pin3, R3.leg2, U1.connector7
  N1: IC1.pin2, R2.Pin_0, U1.connector2
  N2: IC1.pin4, R1.Pin_0
  GND: R1.Pin_1, R2.Pin_1, R3.leg1
  N3: R3.wiper, U1.connector1

notes:
  output
